# Fritzing sketch schematics (saved by Fritzing 0.9.3b)
breadboards: 1

parts:
  Componente1 = Arduino Due (Rev2b)
  KY-1 = Keyes Relay [package=THT]
  R1 = Rotary Potentiometer (Small) [maximum_resistance=100kΩ package=THT]
  R2 = Rotary Potentiometer (Small) [maximum_resistance=100kΩ package=THT]
  R3 = Rotary Potentiometer (Small) [maximum_resistance=100kΩ package=THT]
  S1 = Pushbutton [package="[SMD]"]
  S2 = Pushbutton [package="[SMD]"]
  S3 = Pushbutton [package="[SMD]"]
  S4 = Pushbutton [package="[SMD]"]
  S5 = Pushbutton [package="[SMD]"]
  R4 = Resistor [tolerance=±5% resistance=220 package="0402 [SMD]"]
  LED1 = LED - 3mm [color="Red (633nm)" package="3 mm [THT]"]
  LED2 = LED - 3mm [color="Red (633nm)" package="3 mm [THT]"]
  LED3 = LED - 3mm [color="Red (633nm)" package="3 mm [THT]"]
  R5 = Resistor [tolerance=±5% resistance=220 package="0402 [SMD]"]
  R6 = Resistor [tolerance=±5% resistance=220 package="0402 [SMD]"]
  S6 = Pushbutton [package="[SMD]"]
  S7 = Pushbutton [package="[SMD]"]
  S8 = Pushbutton [package="[SMD]"]
  R7 = Resistor [tolerance=±5% resistance=220 package="0402 [SMD]"]
  R8 = Resistor [tolerance=±5% resistance=220 package="0402 [SMD]"]
  R9 = Resistor [tolerance=±5% resistance=220 package="0402 [SMD]"]
  LED4 = LED - 3mm [color="Red (633nm)" package="3 mm [THT]"]
  LED5 = LED - 3mm [color="Red (633nm)" package="3 mm [THT]"]
  LED6 = LED - 3mm [color="Red (633nm)" package="3 mm [THT]"]
  KY-2 = Keyes Relay [package=THT]
  KY-3 = Keyes Relay [package=THT]
  KY-4 = Keyes Relay [package=THT]
  KY-5 = Keyes Relay [package=THT]

nets:
  N1: Componente1.A0, R1.wiper
  N2: Componente1.A1, R3.wiper
  N3: Componente1.A2, R2.wiper
  N4: Componente1.IOREF, R1.leg1, R2.leg1, R3.leg1
  N5: Componente1.5V, KY-1.power, KY-2.power, KY-3.power, KY-4.power, KY-5.power
  N6: Componente1.GND, R1.leg2, R2.leg2, R3.leg2, S1.Pin_3, S1.Pin_4, S2.Pin_1, S2.Pin_2, S3.Pin_1, S3.Pin_2, S4.Pin_1, S4.Pin_2, S5.Pin_1, S5.Pin_2, S6.Pin_1, S6.Pin_2, S7.Pin_1, S7.Pin_2, S8.Pin_1, S8.Pin_2
  N7: Componente1.D2_PWM, KY-1.NO
  N8: Componente1.D6_PWM, S1.Pin_1, S1.Pin_2
  N9: Componente1.D22, S2.Pin_3, S2.Pin_4
  N10: Componente1.D23, LED5.anode
  N11: Componente1.D24, S3.Pin_3, S3.Pin_4
  N12: Componente1.D25, LED6.anode
  N13: Componente1.D26, S4.Pin_3, S4.Pin_4
  N14: Componente1.D27, LED4.anode
  N15: Componente1.D28, S5.Pin_3, S5.Pin_4
  N16: Componente1.D32, S6.Pin_3, S6.Pin_4
  N17: Componente1.D33, LED2.anode
  N18: Componente1.D34, S7.Pin_3, S7.Pin_4
  N19: Componente1.D35, LED3.anode
  N20: Componente1.D36, S8.Pin_3, S8.Pin_4
  N21: Componente1.D37, LED1.anode
  N22: Componente1.D40, KY-1.signal
  N23: Componente1.D42, KY-2.signal
  N24: Componente1.D44, KY-3.signal
  N25: Componente1.D46, KY-4.signal
  N26: Componente1.D48, KY-5.signal
  N27: KY-1.ground, KY-1.C, R4.Pin_1, R5.Pin_1, R6.Pin_1, R7.Pin_1, R8.Pin_1, R9.Pin_1, KY-2.ground, KY-3.ground, KY-4.ground, KY-5.ground
  N28: R4.Pin_0, LED1.cathode
  N29: LED2.cathode, R5.Pin_0
  N30: LED3.cathode, R6.Pin_0
  N31: R7.Pin_0, LED6.cathode
  N32: R8.Pin_0, LED5.cathode
  N33: R9.Pin_0, LED4.cathode

custom parts:
  Keyes Relay: The Keyes 5V relay module is suitable for SCM development, home appliance control. It uses a 5V~12V TIL control signal which can control DC / AC signal.
